# Fritzing sketch human-interface (saved by Fritzing 0.9.3b)
breadboards: 1

parts:
  U1 = 7-SEGMENT-4DIGIT [package=7-segment-4digit]
  Part1 = Arduino Uno (Rev3) - ICSP
  hc-sr1 = hc-sr04
  S1 = Square Pushbutton
  J1 = Basic Servo

nets:
  N1: U1.1, Part1.D10_PWM/SS
  N2: U1.2, Part1.D9_PWM
  N3: U1.3, Part1.D13/SCK
  N4: U1.4, Part1.D8
  N5: U1.5, Part1.D12/MISO
  N6: U1.6, Part1.D3_PWM
  N7: U1.11, Part1.D7
  N8: U1.13, Part1.D1/TX
  N9: U1.14, Part1.D11_PWM/MOSI
  N10: U1.15, Part1.D6_PWM
  N11: U1.16, Part1.D0/RX
  N12: Part1.A0, hc-sr1.Trig
  N13: Part1.A1, hc-sr1.Echo
  N14: Part1.A5/SCL, S1.leg0
  N15: Part1.D5_PWM, J1.pulse
  VCC: Part1.5V, hc-sr1.VCC, J1.vcc
  GND: Part1.GND, hc-sr1.GND, S1.leg1, J1.gnd
