# Fritzing sketch led-auto (saved by Fritzing 0.9.3b)
breadboards: 1

parts:
  VCC1 = 4 x AAA Battery Mount
  P1 = Trimmer Potentiometer [maximum_resistance=10kΩ package=THT]
  PR1 = PHOTOCELL [package=photocell-kit]
  LED1 = LED - 5mm [color="Red (633nm)" package="5 mm [THT]"]
  R1 = Resistor [tolerance=±5% resistance=1k package=THT]
  R3 = Resistor [tolerance=±5% resistance=10 package=THT]
  R2 = Resistor [tolerance=±5% resistance=220 package=THT]
  Q1 = NPN-Transistor [package="TO92 [THT]"]

nets:
  N1: VCC1.-, R1.Pin_1, R2.Pin_1
  N2: VCC1.+, R3.Pin_1, Q1.C
  N3: P1.leg1, P1.wiper, PR1.P$1, Q1.B
  N4: P1.leg2, R3.Pin_0, R2.Pin_0
  N5: PR1.P$2, LED1.cathode, R1.Pin_0
  N6: LED1.anode, Q1.E
