# Fritzing sketch led-parallel (saved by Fritzing 0.9.3b)
breadboards: 1

parts:
  LED1 = LED - 5mm [color="Red (633nm)" package="5 mm [THT]"]
  R1 = Resistor [tolerance=±5% resistance=1k package=THT]
  VCC1 = 4 x AAA Battery Mount
  LED2 = LED - 5mm [color="Red (633nm)" package="5 mm [THT]"]
  LED3 = LED - 5mm [color="Red (633nm)" package="5 mm [THT]"]

nets:
  N1: LED1.cathode, R1.Pin_1, LED2.cathode, LED3.cathode
  N2: LED1.anode, VCC1.+, LED2.anode, LED3.anode
  N3: R1.Pin_0, VCC1.-
