# Fritzing sketch led-pot-as-resistor (saved by Fritzing 0.9.3b)
breadboards: 1

parts:
  LED1 = LED - 5mm [color="Red (633nm)" package="5 mm [THT]"]
  R1 = Resistor [tolerance=±5% resistance=1k package=THT]
  VCC1 = 4 x AAA Battery Mount
  R2 = Trimmer Potentiometer [maximum_resistance=10kΩ package=THT]

nets:
  N1: LED1.cathode, R1.Pin_1
  N2: LED1.anode, R2.wiper
  N3: R1.Pin_0, VCC1.-
  N4: VCC1.+, R2.leg2
